# Fritzing sketch schematic (saved by Fritzing 0.9.3b)

parts:
  Part1 = Arduino Uno (Rev3)
  S1 = Ponte-H L298N
  M1 = DC Motor
  M2 = DC Motor
  HC-05/06_Bluetooth_Module = Bluetooth HC-06u
  4x_AA_Built-In_Battery_Holder = Battery
  VCC3 = Battery
  Extra_3x_AA_Batteries = Battery Holders [package=battery-aa-kit]
  BAT2 = Battery Holders [package=battery-aa-kit]
  BAT3 = Battery Holders [package=battery-aa-kit]

nets:
  N1: Part1.D11_PWM/MOSI, S1.connector6
  N2: Part1.D12/MISO, S1.connector5
  N3: Part1.D13/SCK, S1.connector4
  N4: Part1.D0/RX, HC-05/06_Bluetooth_Module.connector2
  N5: Part1.D1/TX, HC-05/06_Bluetooth_Module.connector3
  N6: Part1.D3_PWM, S1.connector9
  N7: Part1.D4, S1.connector8
  N8: Part1.D5_PWM, S1.connector7
  N9: Part1.3V3, HC-05/06_Bluetooth_Module.connector0
  N10: Part1.5V, S1.connector3
  N11: Part1.GND, S1.connector2, HC-05/06_Bluetooth_Module.connector1, BAT3.-
  N12: S1.connector1, 4x_AA_Built-In_Battery_Holder.+
  N13: S1.connector10, M1.pin_2
  N14: S1.connector11, M1.pin_1
  N15: S1.connector13, M2.pin_2
  N16: S1.connector14, M2.pin_1
  N17: 4x_AA_Built-In_Battery_Holder.-, VCC3.+
  N18: VCC3.-, Extra_3x_AA_Batteries.+
  N19: Extra_3x_AA_Batteries.-, BAT2.+
  N20: BAT2.-, BAT3.+
